# Fritzing sketch Schaltplan (saved by Fritzing 0.9.9b)
breadboards: 1

parts:
  Gizwits_WiFi_Witty_ESP-12F1 = Gizwits WiFi Witty ESP-12F
  DHT1 = DHT22 Humidity and Temperature Sensor
  WeMos_D1_Mini_Relay_Shield_V1 = WeMos D1 Mini Relay Shield V2
  OLED_I2C1 = OLED 128x64 I2C Monochrome Display
  U1 = V_REG_LD1117VXX [package=78xxl]
  U2 = V_REG_LD1117VXX [package=78xxl]
  M1 = DC Motor
  Bat1 = battery_holder_single_18650
  Bat2 = battery_holder_single_18650
  YwRobot_Power_Supply1 = YwRobot Breadboard Power Supply [part_number=545043]
  USBTTL1 = Micro USB B Plug
  USBTTL2 = USB A Plug
  J1 = 2.1mm Barrel Jack with Terminal Block

nets:
  N1: Gizwits_WiFi_Witty_ESP-12F1.GPIO14, DHT1.DATA
  N2: Gizwits_WiFi_Witty_ESP-12F1.GPIO12, WeMos_D1_Mini_Relay_Shield_V1.D1
  VCC: Gizwits_WiFi_Witty_ESP-12F1.VCC, WeMos_D1_Mini_Relay_Shield_V1.5V, U1.IN, U2.IN
  GND: Gizwits_WiFi_Witty_ESP-12F1.GND, DHT1.GND, WeMos_D1_Mini_Relay_Shield_V1.G, OLED_I2C1.GND, U1.GND, U2.GND
  N3: Gizwits_WiFi_Witty_ESP-12F1.GPIO4, OLED_I2C1.SDA
  N4: Gizwits_WiFi_Witty_ESP-12F1.GPIO5, OLED_I2C1.SCK
  N5: DHT1.VDD, U2.OUT
  N6: WeMos_D1_Mini_Relay_Shield_V1.COM, YwRobot_Power_Supply1.VCC
  N7: WeMos_D1_Mini_Relay_Shield_V1.NO, M1.pin_1
  N8: OLED_I2C1.VDD, U1.OUT
  N9: M1.pin_2, YwRobot_Power_Supply1.GND
  N10: Bat1.+#0, Bat2.+#1
  N11: Bat1.+#1, J1.NEG
  N12: Bat2.+#0, J1.POS
  N13: USBTTL1.usb, USBTTL2.usb

custom parts:
  battery_holder_single_18650: single 18650 battery holder
  YwRobot Breadboard Power Supply: The YwRobot Breadboard Power Supply (MB-V2) has two power rails; they can be 5V or 3V3. Power to the module can be provided through the female USB socket or through the A10 (female) 2.1mm power jack.
